# Fritzing sketch Montage coeur (saved by Fritzing 0.9.3b)
breadboards: 1

parts:
  LED1 = LED - 5mm [color="Red (633nm)" package="5 mm [THT]"]
  LED2 = LED - 5mm [color="Red (633nm)" package="5 mm [THT]"]
  LED3 = LED - 5mm [color="Red (633nm)" package="5 mm [THT]"]
  LED4 = LED - 5mm [color="Red (633nm)" package="5 mm [THT]"]
  LED5 = LED - 5mm [color="Red (633nm)" package="5 mm [THT]"]
  LED6 = LED - 5mm [color="Red (633nm)" package="5 mm [THT]"]
  LED7 = LED - 5mm [color="Red (633nm)" package="5 mm [THT]"]
  LED10 = LED - 5mm [color="Red (633nm)" package="5 mm [THT]"]
  LED12 = LED - 5mm [color="Red (633nm)" package="5 mm [THT]"]
  Composant1 = Arduino Uno (Rev3)
  LED14 = LED - 5mm [color="Red (633nm)" package="5 mm [THT]"]
  R1 = Resistor [tolerance=±5% resistance=220 package=THT]
  R2 = Resistor [tolerance=±5% resistance=220 package=THT]
  R3 = Resistor [tolerance=±5% resistance=220 package=THT]
  R4 = Resistor [tolerance=±5% resistance=220 package=THT]
  R5 = Resistor [tolerance=±5% resistance=220 package=THT]
  R6 = Resistor [tolerance=±5% resistance=220 package=THT]
  R7 = Resistor [tolerance=±5% resistance=220 package=THT]
  R8 = Resistor [tolerance=±5% resistance=220 package=THT]
  R9 = Resistor [tolerance=±5% resistance=220 package=THT]
  R10 = Resistor [tolerance=±5% resistance=220 package=THT]  # not connected

nets:
  N1: LED1.cathode, R8.Pin_1, R9.Pin_0
  N2: LED1.anode, LED2.cathode, LED3.anode, LED4.cathode, LED5.cathode, LED6.anode, LED10.anode, LED12.anode, Composant1.GND, LED14.cathode
  N3: LED4.anode, R5.Pin_0
  N4: LED5.anode, R2.Pin_0
  N5: LED6.cathode, LED7.anode, Composant1.D11_PWM/MOSI, R6.Pin_1
  N6: LED7.cathode, R7.Pin_1
  N7: LED10.cathode, R3.Pin_0
  N8: LED12.cathode, R4.Pin_0
  N9: Composant1.D10_PWM/SS, R9.Pin_1
  N10: Composant1.D12/MISO, R6.Pin_0
  N11: Composant1.D13/SCK, R7.Pin_0
  N12: Composant1.D2, R2.Pin_1
  N13: Composant1.D3_PWM, R1.Pin_1
  N14: Composant1.D4, R5.Pin_1
  N15: Composant1.D5_PWM, R3.Pin_1
  N16: Composant1.D6_PWM, R4.Pin_1
  N17: LED14.anode, R1.Pin_0
